// Logisim project alu.circ as structural Verilog: 1 circuit, main circuit alu
module alu (
  input  [31:0] A,
  input  [31:0] B,
  input  [3:0] ALUSel,
  output [31:0] Result
);

  wire slt7;
  wire [31:0] add0, and1, bit_extender_1_out, bsel13, mul10, mulh14, mulhu11, or2, sll6, sra5, srl4, sub12,
       xor3;

  Adder #(.width(32)) adder_1 (.a(A), .b(B), .out(add0));  // open: cin, cout
  assign and1 = A & B;  // AND_Gate and_1, 32 bits wide
  assign or2 = A | B;  // OR_Gate or_1, 32 bits wide
  assign xor3 = A ^ B;  // XOR_Gate xor_1, 32 bits wide
  Shifter #(.shift("lr"), .width(32)) shifter_1 (.in(A), .\dist (B[4:0]), .out(srl4));
  Shifter #(.shift("ar"), .width(32)) shifter_2 (.in(A), .\dist (B[4:0]), .out(sra5));
  Shifter #(.width(32)) shifter_3 (.in(A), .\dist (B[4:0]), .out(sll6));
  Comparator #(.width(32)) comparator_1 (.a(A), .b(B), .lt(slt7));  // open: gt, eq
  Multiplier #(.mode("twosComplement"), .width(32)) multiplier_1 (
    .a(A), .b(B), .out(mul10), .cout(mulh14));  // open: cin
  Multiplier #(.width(32)) multiplier_2 (.a(A), .b(B), .cout(mulhu11));  // open: out, cin
  Subtractor #(.width(32)) subtractor_1 (.a(A), .b(B), .out(sub12));  // open: bin, bout
  Multiplexer #(.enable("false"), .width(32)) multiplexer_1 (.in0(A), .in1(B), .out(bsel13), .sel(1'b1));
  Multiplexer #(.enable("false"), .select(4), .width(32)) multiplexer_2 (
    .in0(add0), .in1(and1), .in2(or2), .in3(xor3), .in4(srl4), .in5(sra5), .in6(sll6),
    .in7(bit_extender_1_out), .in10(mul10), .in11(mulhu11), .in12(sub12), .in13(bsel13), .in14(mulh14),
    .out(Result), .sel(ALUSel));  // open: in8, in9, in15
  assign bit_extender_1_out = {{31{1'b0}}, slt7};  // Bit_Extender bit_extender_1

  // Notes on the sheet:
  //   INPUTS to your circuit
  //   DON'T CHANGE THE LOCATIONS OF THE INPUTS AND OUTPUTS!
  //   OUTPUT from your circuit
endmodule
