// Logisim project control_logic.circ as structural Verilog: 2 circuits, main circuit control_logic
module control_logic (
  input  [31:0] inst,
  input  BrEq,
  input  BrLt,
  output PCSel,
  output RegWEn,
  output [2:0] ImmSel,
  output BrUn,
  output ASel,
  output BSel,
  output [3:0] ALUSel,
  output MemRW,
  output [1:0] WBSel,
  output CSRSel,
  output CSRWen
);

  wire and_1_out, and_2_out, and_3_out, and_4_out, and_5_out, and_6_out, and_7_out, and_8_out, and_11_out,
       and_12_out, and_14_out, and_16_out, and_22_out, and_24_out, and_25_out, and_26_out, base_i, branch,
       comparator_1_eq, comparator_2_eq, comparator_3_eq, comparator_4_eq, comparator_5_eq, comparator_6_eq,
       comparator_7_eq, comparator_8_eq, comparator_9_eq, comparator_10_eq, comparator_11_eq,
       comparator_12_eq, comparator_13_eq, comparator_14_eq, comparator_15_eq, comparator_16_eq,
       comparator_17_eq, comparator_18_eq, comparator_19_eq, comparator_20_eq, comparator_21_eq,
       comparator_23_eq, is_and, is_lui, is_mul, is_mulh, is_mulhu, is_or, is_sll, is_slt, is_sra, is_srl,
       is_sub, is_xor, jal, jalr, load, not_1_out, not_2_out, or_1_out, or_2_out, or_3_out, or_6_out,
       or_13_out, R, U;
  wire [2:0] funct3, multiplexer_1_out, multiplexer_2_out, multiplexer_3_out, multiplexer_4_out,
       multiplexer_5_out;
  wire [6:0] funct7, opcode;
  wire [31:0] shifter_1_out, shifter_2_out;

  Bit_Extender #(.in_width(32), .out_width(7)) bit_extender_1 (.in(inst), .out(opcode));
  Shifter #(.shift("lr"), .width(32)) shifter_1 (.in(inst), .\dist (5'b01100), .out(shifter_1_out));
  Shifter #(.shift("lr"), .width(32)) shifter_2 (.in(inst), .\dist (5'b11001), .out(shifter_2_out));
  Bit_Extender #(.in_width(32), .out_width(3), .\type ("zero")) bit_extender_2 (.in(shifter_1_out), .out(funct3));
  Bit_Extender #(.in_width(32), .out_width(7), .\type ("zero")) bit_extender_3 (.in(shifter_2_out), .out(funct7));
  not not_1 (not_1_out, BrEq);
  and and_1 (and_1_out, not_1_out, not_2_out);
  not not_2 (not_2_out, BrLt);
  judg_type judg_type_1 (
    .opcode(opcode), .R(R), .load(load), .base_i(base_i), .store(MemRW), .branch(branch), .U(U), .jal(jal),
    .jalr(jalr), .csr(CSRWen));
  Comparator #(.mode("unsigned"), .width(3)) comparator_1 (
    .a(funct3), .b(3'b000), .eq(comparator_1_eq));  // open: gt, lt
  Comparator #(.mode("unsigned"), .width(3)) comparator_2 (
    .a(funct3), .b(3'b001), .eq(comparator_2_eq));  // open: gt, lt
  Comparator #(.mode("unsigned"), .width(3)) comparator_3 (
    .a(funct3), .b(3'b100), .eq(comparator_3_eq));  // open: gt, lt
  Comparator #(.mode("unsigned"), .width(3)) comparator_4 (
    .a(funct3), .b(3'b101), .eq(comparator_4_eq));  // open: gt, lt
  Comparator #(.mode("unsigned"), .width(3)) comparator_5 (
    .a(funct3), .b(3'b110), .eq(comparator_5_eq));  // open: gt, lt
  Comparator #(.mode("unsigned"), .width(3)) comparator_6 (
    .a(funct3), .b(3'b111), .eq(comparator_6_eq));  // open: gt, lt
  and and_2 (and_2_out, comparator_1_eq, BrEq);
  and and_3 (and_3_out, comparator_2_eq, not_1_out);
  and and_4 (and_4_out, comparator_3_eq, BrLt);
  and and_5 (and_5_out, comparator_4_eq, and_1_out);
  and and_6 (and_6_out, comparator_5_eq, BrLt);
  and and_7 (and_7_out, comparator_6_eq, and_1_out);
  not not_3 (BSel, R);
  or or_1 (or_1_out, and_2_out, and_3_out, and_4_out, and_5_out, and_6_out, and_7_out);
  and and_8 (and_8_out, funct3[2], funct3[1]);
  Comparator #(.mode("unsigned"), .width(7)) comparator_7 (
    .a(opcode), .b(7'b0010111), .eq(comparator_7_eq));  // open: gt, lt
  and and_9 (BrUn, branch, and_8_out);
  or or_2 (or_2_out, MemRW, branch, CSRWen);
  not not_4 (RegWEn, or_2_out);
  and and_10 (CSRSel, CSRWen, funct3[2]);
  or or_3 (or_3_out, jal, jalr);
  and and_11 (and_11_out, branch, or_1_out);
  or or_4 (ASel, branch, jal, comparator_7_eq);
  or or_5 (PCSel, or_3_out, and_11_out);
  or or_6 (or_6_out, load, base_i, jalr, CSRWen);
  or or_7 (WBSel[0], U, R, base_i);
  or or_8 (WBSel[1], jal, jalr);
  or or_9 (ALUSel[2], is_sub, is_mulh, is_lui, is_sll, is_slt, is_sra, is_srl);
  or or_10 (ALUSel[0], is_and, is_lui, is_mulhu, is_slt, is_sra, is_xor);
  Multiplexer #(.enable("false"), .width(3)) multiplexer_1 (
    .in0(3'b000), .in1(3'b000), .out(multiplexer_1_out), .sel(or_6_out));
  Multiplexer #(.enable("false"), .width(3)) multiplexer_2 (
    .in0(3'b000), .in1(3'b001), .out(multiplexer_2_out), .sel(MemRW));
  Multiplexer #(.enable("false"), .width(3)) multiplexer_3 (
    .in0(3'b000), .in1(3'b010), .out(multiplexer_3_out), .sel(branch));
  Multiplexer #(.enable("false"), .width(3)) multiplexer_4 (
    .in0(3'b000), .in1(3'b011), .out(multiplexer_4_out), .sel(U));
  Multiplexer #(.enable("false"), .width(3)) multiplexer_5 (
    .in0(3'b000), .in1(3'b100), .out(multiplexer_5_out), .sel(jal));
  and and_12 (and_12_out, R, comparator_8_eq);
  Comparator #(.mode("unsigned"), .width(7)) comparator_8 (
    .a(funct7), .b(7'b0000001), .eq(comparator_8_eq));  // open: gt, lt
  or or_11 (ALUSel[3], and_12_out, is_lui, is_sub);
  ExactlyOne xor_1[2:0] (
    .out(ImmSel), .in0(multiplexer_1_out), .in1(multiplexer_2_out), .in2(multiplexer_3_out),
    .in3(multiplexer_4_out), .in4(multiplexer_5_out));
  or or_12 (ALUSel[1], is_mul, is_mulhu, is_xor, is_or, is_sll, is_slt);
  Comparator #(.mode("unsigned"), .width(7)) comparator_9 (
    .a(funct7), .b(7'b0000001), .eq(comparator_9_eq));  // open: gt, lt
  Comparator #(.mode("unsigned"), .width(3)) comparator_10 (
    .a(funct3), .b(3'b001), .eq(comparator_10_eq));  // open: gt, lt
  Comparator #(.mode("unsigned"), .width(7)) comparator_11 (
    .a(funct7), .b({7{1'b0}}), .eq(comparator_11_eq));  // open: gt, lt
  Comparator #(.mode("unsigned"), .width(3)) comparator_12 (
    .a(funct3), .b(3'b101), .eq(comparator_12_eq));  // open: gt, lt
  Comparator #(.mode("unsigned"), .width(7)) comparator_13 (
    .a(funct7), .b({7{1'b0}}), .eq(comparator_13_eq));  // open: gt, lt
  Comparator #(.mode("unsigned"), .width(7)) comparator_14 (
    .a(funct7), .b(7'b0100000), .eq(comparator_14_eq));  // open: gt, lt
  and and_13 (is_mulh, and_14_out, R);
  and and_14 (and_14_out, comparator_9_eq, comparator_10_eq);
  and and_15 (is_sll, and_16_out, or_13_out);
  and and_16 (and_16_out, comparator_10_eq, comparator_11_eq);
  and and_17 (is_slt, comparator_15_eq, or_13_out);
  Comparator #(.mode("unsigned"), .width(3)) comparator_15 (
    .a(funct3), .b(3'b010), .eq(comparator_15_eq));  // open: gt, lt
  and and_18 (is_xor, comparator_16_eq, or_13_out);
  Comparator #(.mode("unsigned"), .width(3)) comparator_16 (
    .a(funct3), .b(3'b100), .eq(comparator_16_eq));  // open: gt, lt
  and and_19 (is_or, comparator_17_eq, or_13_out);
  Comparator #(.mode("unsigned"), .width(3)) comparator_17 (
    .a(funct3), .b(3'b110), .eq(comparator_17_eq));  // open: gt, lt
  and and_20 (is_and, comparator_18_eq, or_13_out);
  Comparator #(.mode("unsigned"), .width(3)) comparator_18 (
    .a(funct3), .b(3'b111), .eq(comparator_18_eq));  // open: gt, lt
  and and_21 (is_srl, and_22_out, or_13_out);
  and and_22 (and_22_out, comparator_12_eq, comparator_13_eq);
  and and_23 (is_sra, and_24_out, or_13_out);
  and and_24 (and_24_out, comparator_12_eq, comparator_14_eq);
  or or_13 (or_13_out, R, base_i);
  Comparator #(.mode("unsigned"), .width(3)) comparator_19 (
    .a(funct3), .b(3'b000), .eq(comparator_19_eq));  // open: gt, lt
  and and_25 (and_25_out, comparator_19_eq, comparator_20_eq);
  Comparator #(.mode("unsigned"), .width(7)) comparator_20 (
    .a(funct7), .b(7'b0000001), .eq(comparator_20_eq));  // open: gt, lt
  and and_26 (and_26_out, comparator_19_eq, comparator_21_eq);
  Comparator #(.mode("unsigned"), .width(7)) comparator_21 (
    .a(funct7), .b(7'b0100000), .eq(comparator_21_eq));  // open: gt, lt
  Comparator #(.mode("unsigned"), .width(7)) comparator_22 (.a(opcode), .b(7'b0110111), .eq(is_lui));  // open: gt, lt
  and and_27 (is_mul, and_25_out, R);
  and and_28 (is_sub, and_26_out, R);
  and and_29 (is_mulhu, comparator_23_eq, R);
  Comparator #(.mode("unsigned"), .width(3)) comparator_23 (
    .a(funct3), .b(3'b011), .eq(comparator_23_eq));  // open: gt, lt

  // Other names for the same wires on the sheet: ALUSel_0 = ALUSel[0]; ALUSel_1 = ALUSel[1]; ALUSel_2 = ALUSel[2];
  //   ALUSel_3 = ALUSel[3]; csr = CSRWen; store = MemRW

  // Notes on the sheet:
  //   INPUTS to your circuit
  //   DON'T CHANGE THE LOCATIONS OF THE INPUTS AND OUTPUTS!
  //   OUTPUT from your circuit
endmodule

module judg_type (
  input  [6:0] opcode,
  output R,
  output load,
  output base_i,
  output store,
  output branch,
  output U,
  output jal,
  output jalr,
  output csr
);

  wire comparator_6_eq, comparator_7_eq;

  Comparator #(.mode("unsigned"), .width(7)) comparator_1 (.a(opcode), .b(7'b0110011), .eq(R));  // open: gt, lt
  Comparator #(.mode("unsigned"), .width(7)) comparator_2 (.a(opcode), .b(7'b0000011), .eq(load));  // open: gt, lt
  Comparator #(.mode("unsigned"), .width(7)) comparator_3 (.a(opcode), .b(7'b0010011), .eq(base_i));  // open: gt, lt
  Comparator #(.mode("unsigned"), .width(7)) comparator_4 (.a(opcode), .b(7'b0100011), .eq(store));  // open: gt, lt
  Comparator #(.mode("unsigned"), .width(7)) comparator_5 (.a(opcode), .b(7'b1100011), .eq(branch));  // open: gt, lt
  Comparator #(.mode("unsigned"), .width(7)) comparator_6 (
    .a(opcode), .b(7'b0010111), .eq(comparator_6_eq));  // open: gt, lt
  Comparator #(.mode("unsigned"), .width(7)) comparator_7 (
    .a(opcode), .b(7'b0110111), .eq(comparator_7_eq));  // open: gt, lt
  Comparator #(.mode("unsigned"), .width(7)) comparator_8 (.a(opcode), .b(7'b1101111), .eq(jal));  // open: gt, lt
  Comparator #(.mode("unsigned"), .width(7)) comparator_9 (.a(opcode), .b(7'b1100111), .eq(jalr));  // open: gt, lt
  Comparator #(.mode("unsigned"), .width(7)) comparator_10 (.a(opcode), .b(7'b1110011), .eq(csr));  // open: gt, lt
  or or_1 (U, comparator_6_eq, comparator_7_eq);
endmodule
