// Logisim project cpu.circ as structural Verilog: 1 circuit, main circuit cpu
module cpu (
  input  clk,
  input  [31:0] INSTRUCTION,
  input  [31:0] READ_DATA,
  output [31:0] WRITE_ADDRESS,
  output [31:0] PROGRAM_COUNTER,
  output [31:0] ra,
  output [31:0] sp,
  output [31:0] t0,
  output [31:0] t1,
  output [31:0] t2,
  output [31:0] s0,
  output [31:0] s1,
  output [31:0] a0,
  output [31:0] tohost,
  output [3:0] WRITE_ENABLE,
  output [31:0] WRITE_DATA
);

  wire ASel, BrEq, BrLt, BrUn, BSel, CSRSel, CSRWen, MemRW, PCSel, RegWEn;
  wire [1:0] WBSel;
  wire [2:0] ImmSel;
  wire [3:0] ALUSel;
  wire [31:0] adder_2_out, bit_extender_2_out, CSRDin, fetch_addr, imm, INSTRUCTION_OLD, multiplexer_1_out,
       multiplexer_3_out, multiplexer_4_out, PC, PCadd4, RegWriteData, rs1_value;

  Adder #(.width(32)) adder_1 (.a(PROGRAM_COUNTER), .b(32'h4), .out(PCadd4));  // open: cin, cout
  Register #(.width(32)) u_PC (.D(fetch_addr), .en(1'b1), .clk(clk), .Q(PROGRAM_COUNTER));  // open: clr
  Register #(.width(32)) PC_old (.D(PROGRAM_COUNTER), .en(1'b1), .clk(clk), .Q(PC));  // open: clr
  Register #(.width(32)) IR (.D(multiplexer_1_out), .en(1'b1), .clk(clk), .Q(INSTRUCTION_OLD));  // open: clr
  Multiplexer #(.enable("false"), .width(32)) multiplexer_1 (
    .in0(INSTRUCTION), .in1(32'h13), .out(multiplexer_1_out), .sel(PCSel));
  Multiplexer #(.enable("false"), .width(32)) multiplexer_2 (
    .in0(PCadd4), .in1(WRITE_ADDRESS), .out(fetch_addr), .sel(PCSel));
  control_logic control_logic_1 (
    .CSRWen(CSRWen), .PCSel(PCSel), .RegWEn(RegWEn), .ImmSel(ImmSel), .BrUn(BrUn), .ASel(ASel), .BSel(BSel),
    .ALUSel(ALUSel), .MemRW(MemRW), .WBSel(WBSel), .CSRSel(CSRSel), .inst(INSTRUCTION_OLD), .BrEq(BrEq),
    .BrLt(BrLt));
  regfile regfile_1 (
    .rs1(INSTRUCTION_OLD[19:15]), .rs2(INSTRUCTION_OLD[24:20]), .rd(INSTRUCTION_OLD[11:7]),
    .Write_Data(RegWriteData), .RegWEn(RegWEn), .clk(clk), .ra(ra), .sp(sp), .t0(t0), .t1(t1), .t2(t2),
    .s0(s0), .s1(s1), .a0(a0), .Read_Data_1(rs1_value), .Read_Data_2(WRITE_DATA));
  branch_comp branch_comp_1 (.rs1(rs1_value), .rs2(WRITE_DATA), .BrUn(BrUn), .BrEq(BrEq), .BrLt(BrLt));
  imm_gen imm_gen_1 (.inst(INSTRUCTION_OLD), .ImmSel(ImmSel), .imm(imm));
  assign WRITE_ENABLE = {{3{MemRW}}, MemRW};  // Bit_Extender bit_extender_1
  assign bit_extender_2_out = {{27{1'b0}}, INSTRUCTION_OLD[19:15]};  // Bit_Extender bit_extender_2
  Multiplexer #(.enable("false"), .width(32)) multiplexer_3 (
    .in0(rs1_value), .in1(PC), .out(multiplexer_3_out), .sel(ASel));
  Multiplexer #(.enable("false"), .width(32)) multiplexer_4 (
    .in0(WRITE_DATA), .in1(imm), .out(multiplexer_4_out), .sel(BSel));
  csr csr_1 (.CSR_address(12'h51e), .CSR_din(CSRDin), .CSR_WE(CSRWen), .clk(clk), .tohost(tohost));
  Multiplexer #(.enable("false"), .width(32)) multiplexer_5 (
    .in0(rs1_value), .in1(bit_extender_2_out), .out(CSRDin), .sel(CSRSel));
  alu alu_1 (.Result(WRITE_ADDRESS), .A(multiplexer_3_out), .B(multiplexer_4_out), .ALUSel(ALUSel));
  Adder #(.width(32)) adder_2 (.a(PC), .b(32'h4), .out(adder_2_out));  // open: cin, cout
  Multiplexer #(.enable("false"), .select(2), .width(32)) multiplexer_6 (
    .in0(READ_DATA), .in1(WRITE_ADDRESS), .in2(adder_2_out), .out(RegWriteData), .sel(WBSel));  // open: in3

  // Other names for the same wires on the sheet: alu_result[31:0] = WRITE_ADDRESS; rd[4:0] = INSTRUCTION_OLD[11:7];
  //   rs1[4:0] = INSTRUCTION_OLD[19:15]; rs2[4:0] = INSTRUCTION_OLD[24:20]; rs2_value[31:0] = WRITE_DATA

  // Notes on the sheet:
  //   Output to IMEM
  //   IMEM (do **NOT** move this)
  //   Inputs from IMEM
  //   It is OK to move the PC, RegFile, ALU, MEM, Branch Comp, Imm Gen, and Control Logic to wherever is most convenient for you when constructing your CPU, and to delete this text
  //   Inputs/Outputs for testing. Do **NOT** move these.
  //   Outputs To DMEM
  //   DMEM (do **NOT** move this)
  //   Inputs From DMEM
endmodule
