// Logisim project imm_gen.circ as structural Verilog: 1 circuit, main circuit imm_gen
module imm_gen (
  input  [31:0] inst,
  input  [2:0] ImmSel,
  output [31:0] imm
);

  wire [31:0] imm_I, imm_U, shifter_2_out;
  wire [31:5] imm_S;
  wire [31:12] imm_B;
  wire [31:20] imm_J;

  Shifter #(.shift("ar"), .width(32)) shifter_1 (.in(inst), .\dist (5'b10100), .out(imm_I));
  assign imm_S = {{20{inst[31]}}, inst[31:25]};  // Bit_Extender bit_extender_1
  assign imm_B = {{19{inst[31]}}, inst[31]};  // Bit_Extender bit_extender_2
  Shifter #(.shift("ar"), .width(32)) shifter_2 (.in(inst), .\dist (5'b01100), .out(shifter_2_out));
  assign imm_J = {{11{inst[31]}}, inst[31]};  // Bit_Extender bit_extender_3
  Shifter #(.width(32)) shifter_3 (.in(shifter_2_out), .\dist (5'b01100), .out(imm_U));
  Multiplexer #(.enable("false"), .select(3), .width(32)) multiplexer_1 (
    .in0(imm_I), .in1({imm_S, inst[11:7]}), .in2({imm_B, inst[7], inst[30:25], inst[11:8], 1'b0}),
    .in3(imm_U), .in4({imm_J, inst[19:12], inst[20], inst[30:21], 1'b0}), .out(imm), .sel(ImmSel));  // open: in5, in6, in7

  // Other names for the same wires on the sheet: imm_B[11:1] = {inst[7], inst[30:25], inst[11:8]};
  //   imm_S[4:0] = inst[11:7]; imm_J[19:1] = {inst[19:12], inst[20], inst[30:21]}

  // Notes on the sheet:
  //   INPUTS to your circuit
  //   DON'T CHANGE THE LOCATIONS OF THE INPUTS AND OUTPUTS!
  //   OUTPUT from your circuit
endmodule
